// Logisim project ALUwithFlag.circ as structural Verilog: 4 circuits, main circuit main
module main (
  input  S0,
  input  S1,
  input  S2,
  input  in_4,
  input  in_5,
  input  in_6,
  output S2_prime_S1_prime_S0_prime,
  output S2_prime_S1_prime_S0,
  output S2_prime_S1S0_prime,
  output S2_prime_S1S0,
  output S2S1_prime_S0_prime,
  output S2S1_prime_S0,
  output S2S1S0_prime,
  output S2S1S0
);

  // _74238 74238_1: pin names not known; wires that end beside it: S0, S1, S2, in_4, in_5, in_6, S2S1S0, 1'b0, 1'b1, S2_prime_S1_prime_S0_prime, S2_prime_S1_prime_S0, S2_prime_S1S0_prime, S2_prime_S1S0, S2S1_prime_S0_prime, S2S1_prime_S0, S2S1S0_prime
endmodule

module demo2 (
  input  S0,
  input  S1,
  input  S2,
  input  E0,
  input  E0_2,
  input  E1,
  input  A0,
  input  A1,
  input  A2,
  input  A3,
  input  B0,
  input  B1,
  input  B2,
  input  B3,
  output X0,
  output Z0,
  output Y0,
  output S0_2,
  output X1,
  output S1_2,
  output S2_2,
  output S3,
  output Y1,
  output Cout,
  output Z,
  output C,
  output S,
  output V,
  output X2,
  output Y2,
  output X3,
  output Y3
);

  wire adder_ckt_1__6__s2, adder_ckt_1_cout, adder_ckt_2_cout, main_1_s2_prime_s1_prime_s0,
       main_1_s2_prime_s1_prime_s0_prime, main_1_s2_prime_s1s0, main_1_s2_prime_s1s0_prime,
       main_1_s2s1_prime_s0, main_1_s2s1_prime_s0_prime, main_1_s2s1s0, main_1_s2s1s0_prime, n7404_1_p2,
       n7404_1_p3, n7404_1_p6, n7404_1_p7, n7404_1_p8, n7404_1_p9, n7404_1_p10, n7404_1_p12, n7408_1_p1,
       n7408_1_p6, n7408_1_p8, n7408_1_p12, n7408_2_p1, n7408_2_p6, n7408_2_p8, n7408_2_p12, n7408_3_p3,
       n7408_3_p6, n7408_3_p12, n7408_4_p9, n7408_4_p12, n7432_1_p6, n7432_1_p8, n7432_2_p6, n7432_2_p8,
       n7432_3_p6, n7432_3_p8, n7432_4_p6, n7432_4_p8, n7432_5_p3, n7432_5_p6;

  main main_1 (
    .S0(S0), .S1(S1), .S2(S2), .in_4(E0), .in_5(E0_2), .in_6(E1),
    .S2_prime_S1_prime_S0_prime(main_1_s2_prime_s1_prime_s0_prime),
    .S2_prime_S1_prime_S0(main_1_s2_prime_s1_prime_s0), .S2_prime_S1S0_prime(main_1_s2_prime_s1s0_prime),
    .S2_prime_S1S0(main_1_s2_prime_s1s0), .S2S1_prime_S0_prime(main_1_s2s1_prime_s0_prime),
    .S2S1_prime_S0(main_1_s2s1_prime_s0), .S2S1S0_prime(main_1_s2s1s0_prime), .S2S1S0(main_1_s2s1s0));
  // _7408 7408_1: pin names not known; wires that end beside it: n7408_1_p1, B0, Y0, main_1_s2s1_prime_s0, B0, n7408_1_p6, B1, n7408_1_p8, Y1, main_1_s2s1_prime_s0, B1, n7408_1_p12
  // _7408 7408_2: pin names not known; wires that end beside it: n7408_2_p1, B2, Y2, main_1_s2s1_prime_s0, B2, n7408_2_p6, B3, n7408_2_p8, Y3, main_1_s2s1_prime_s0, B3, n7408_2_p12
  // _7432 7432_1: pin names not known; wires that end beside it: A0, n7408_1_p6, X0, main_1_s2_prime_s1_prime_s0_prime, main_1_s2_prime_s1_prime_s0, n7432_1_p6, main_1_s2s1s0, n7432_1_p8, n7408_1_p1, main_1_s2s1_prime_s0_prime, n7432_1_p6, n7432_1_p8
  // _7432 7432_2: pin names not known; wires that end beside it: A1, n7408_1_p12, X1, main_1_s2_prime_s1_prime_s0_prime, main_1_s2_prime_s1_prime_s0, n7432_2_p6, main_1_s2s1s0, n7432_2_p8, n7408_1_p8, main_1_s2s1_prime_s0_prime, n7432_2_p6, n7432_2_p8
  // _7432 7432_3: pin names not known; wires that end beside it: A2, n7408_2_p6, X2, main_1_s2_prime_s1_prime_s0_prime, main_1_s2_prime_s1_prime_s0, n7432_3_p6, main_1_s2s1s0, n7432_3_p8, n7408_2_p1, main_1_s2s1_prime_s0_prime, n7432_3_p6, n7432_3_p8
  // _7432 7432_4: pin names not known; wires that end beside it: A3, n7408_2_p12, X3, main_1_s2_prime_s1_prime_s0_prime, main_1_s2_prime_s1_prime_s0, n7432_4_p6, main_1_s2s1s0, n7432_4_p8, n7408_2_p8, main_1_s2s1_prime_s0_prime, n7432_4_p6, n7432_4_p8
  // _7404 7404_1: pin names not known; wires that end beside it: S2, n7404_1_p2, n7404_1_p3, Z, C, n7404_1_p6, n7404_1_p7, n7404_1_p8, n7404_1_p9, n7404_1_p10, S0, n7404_1_p12, main_1_s2_prime_s1_prime_s0_prime, main_1_s2_prime_s1_prime_s0, main_1_s2_prime_s1s0_prime, main_1_s2_prime_s1s0, main_1_s2s1_prime_s0_prime, main_1_s2s1_prime_s0, main_1_s2s1s0_prime, main_1_s2s1s0
  Adder_Ckt adder_ckt_1 (
    ._1__A4(X1), ._3__A3(n7408_3_p3), ._4__B3(n7408_3_p3), ._6__S2(adder_ckt_1__6__s2), ._7__B2(1'b0),
    ._8__A2(1'b0), ._16__B4(Y1), ._15__S4(S1_2), .Cout(adder_ckt_1_cout), ._13__Cin(Z0), ._11__B1(Y0),
    ._10__A1(X0), ._9__S1(S0_2));  // open: _2__S3, _5__Vcc, _12__GND
  Adder_Ckt adder_ckt_2 (
    ._1__A4(X3), ._3__A3(n7408_3_p6), ._4__B3(n7408_3_p6), ._6__S2(n7404_1_p9), ._7__B2(1'b0), ._8__A2(1'b0),
    ._16__B4(Y3), ._15__S4(S), .Cout(adder_ckt_2_cout), ._13__Cin(n7408_3_p12), ._11__B1(Y2), ._10__A1(X2),
    ._9__S1(S2_2));  // open: _2__S3, _5__Vcc, _12__GND
  // _7408 7408_3: pin names not known; wires that end beside it: n7404_1_p8, adder_ckt_1__6__s2, n7408_3_p3, n7404_1_p9, n7404_1_p8, n7408_3_p6, n7404_1_p2, S0, Z0, n7404_1_p8, adder_ckt_1_cout, n7408_3_p12
  // _7408 7408_4: pin names not known; wires that end beside it: adder_ckt_2_cout, n7404_1_p8, C, S2, S0, n7404_1_p7, n7404_1_p10, C, n7408_4_p9, n7404_1_p9, n7404_1_p6, n7408_4_p12
  // _7432 7432_5: pin names not known; wires that end beside it: S0_2, S1_2, n7432_5_p3, n7432_5_p3, S2_2, n7432_5_p6, n7408_4_p12, n7408_4_p9, V, S, n7432_5_p6, n7404_1_p3

  assign Cout = C;
  assign S3 = S;
endmodule

module adderckt (
  input  A0,
  input  B3,
  input  B2,
  input  B1,
  input  B0,
  input  A3,
  input  A2,
  input  A1,
  input  S2,
  input  S1,
  input  S0,
  output out_12
);

  wire demo2_1_p11, demo2_1_p12, demo2_1_p13, n7404_1_p6;

  // demo2 demo2_1: pin names not known; wires that end beside it: B3, A3, B2, A2, B1, A1, B0, A0, 1'b1, 1'b0, demo2_1_p11, demo2_1_p12, demo2_1_p13
  // _7404 7404_1: pin names not known; wires that end beside it: demo2_1_p11, demo2_1_p12, S1, demo2_1_p13, S2, n7404_1_p6
  // _7408 7408_1: pin names not known; wires that end beside it: n7404_1_p6, S0, out_12
endmodule

module Adder_Ckt (
  input  _1__A4,
  input  _16__B4,
  input  _3__A3,
  input  _4__B3,
  input  _13__Cin,
  input  _5__Vcc,
  input  _12__GND,
  input  _11__B1,
  input  _7__B2,
  input  _10__A1,
  input  _8__A2,
  output _2__S3,
  output _15__S4,
  output Cout,
  output _6__S2,
  output _9__S1
);

  wire and_1_out, and_2_out, and_3_out, and_4_out, and_5_out, and_6_out, and_7_out, and_8_out, and_9_out,
       and_10_out, and_11_out, and_12_out, and_13_out, and_14_out, nand_1_out, nand_2_out, nand_3_out,
       nand_4_out, nor_1_out, nor_2_out, nor_3_out, nor_4_out, nor_6_out, nor_7_out, nor_8_out, not_1_out,
       not_2_out, not_3_out, not_4_out, not_5_out, not_6_out;

  nand nand_1 (nand_1_out, _16__B4, _1__A4);
  nor nor_1 (nor_1_out, _16__B4, _1__A4);
  nand nand_2 (nand_2_out, _4__B3, _3__A3);
  nor nor_2 (nor_2_out, _4__B3, _3__A3);
  nand nand_3 (nand_3_out, _7__B2, _8__A2);
  nor nor_3 (nor_3_out, _7__B2, _8__A2);
  nand nand_4 (nand_4_out, _11__B1, _10__A1);
  nor nor_4 (nor_4_out, _11__B1, _10__A1);
  and and_1 (and_1_out, nor_2_out, nand_1_out);
  and and_2 (and_2_out, nor_3_out, nand_1_out, nand_2_out);
  and and_3 (and_3_out, nor_4_out, nand_1_out, nand_2_out, nand_3_out);
  and and_4 (and_4_out, nand_1_out, nand_2_out, nand_3_out, nand_4_out, not_2_out);
  not not_1 (not_1_out, nor_1_out);
  and and_5 (and_5_out, nor_3_out, nand_2_out);
  and and_6 (and_6_out, nor_4_out, nand_2_out, nand_3_out);
  and and_7 (and_7_out, nand_2_out, nand_3_out, nand_4_out, not_2_out);
  not not_2 (not_2_out, _13__Cin);
  not not_3 (not_3_out, nor_2_out);
  and and_8 (and_8_out, nor_4_out, nand_3_out);
  and and_9 (and_9_out, nand_3_out, nand_4_out, not_2_out);
  not not_4 (not_4_out, nor_3_out);
  and and_10 (and_10_out, nand_4_out, not_2_out);
  not not_5 (not_5_out, nor_4_out);
  not not_6 (not_6_out, not_2_out);
  nor nor_5 (Cout, nor_1_out, and_1_out, and_2_out, and_3_out, and_4_out);
  and and_11 (and_11_out, nand_1_out, not_1_out);
  and and_12 (and_12_out, nand_2_out, not_3_out);
  and and_13 (and_13_out, nand_3_out, not_4_out);
  and and_14 (and_14_out, nand_4_out, not_5_out);
  xor xor_1 (_15__S4, and_11_out, nor_6_out);
  nor nor_6 (nor_6_out, nor_2_out, and_5_out, and_6_out, and_7_out);
  xor xor_2 (_2__S3, and_12_out, nor_7_out);
  nor nor_7 (nor_7_out, nor_3_out, and_8_out, and_9_out);
  xor xor_3 (_6__S2, and_13_out, nor_8_out);
  nor nor_8 (nor_8_out, nor_4_out, and_10_out);
  xor xor_4 (_9__S1, and_14_out, not_6_out);
endmodule
