// Logisim project EncoderLib.circ as structural Verilog: 3 circuits, main circuit 8x3 Priority Encoder
// 8X3PE
module _8x3_Priority_Encoder (
  input  I7,
  input  I6,
  input  I5,
  input  I4,
  input  I3,
  input  I2,
  input  I1,
  input  I0,
  output O2,
  output O1,
  output O0,
  output Va
);

  wire n7432_1_p3, n7432_1_p6, n7432_1_p9, n7432_1_p11, n7432_2_p3, n7432_2_p7;

  // _7432 7432_1: pin names not known; wires that end beside it: I7, I6, n7432_1_p3, n7432_1_p3, I5, n7432_1_p6, 1'b0, 1'b1, n7432_1_p9, I3, n7432_1_p11, I4, n7432_1_p6, n7432_1_p9
  // _7432 7432_2: pin names not known; wires that end beside it: n7432_1_p11, I2, n7432_2_p3, n7432_2_p3, I1, 1'b1, n7432_2_p7, I0, Va
  // _74147 74147_1: pin names not known; wires that end beside it: I3, I4, I5, I6, I7, O2, O1, 1'b0, n7432_2_p7, 1'b0, 1'b1, I2, I1, I0, 1'b0, O0
endmodule

// Shifter
module ShiftFinder (
  input  [31:0] I,
  output Va,
  output [4:0] O
);

  wire n4mux4x1_1_p16, n4mux4x1_1_p17, n4x2_priority_encoder_1_o0, n4x2_priority_encoder_1_o1, n7432_1_p2,
       n7432_1_p3, n7432_1_p4, n7432_1_p6, n7432_1_p7, n7432_1_p8, n7432_1_p12, PE1_o2, PE2_o2, PE3_o2;
  wire [1:0] n4mux4x1_1_p15, PE0_o0, PE1_o0, PE2_o0, PE3_o0;

  // _7432 7432_1: pin names not known; wires that end beside it: 1'b1, n7432_1_p2, n7432_1_p3, n7432_1_p4, n7432_1_p4, n7432_1_p6, n7432_1_p7, n7432_1_p8, n7432_1_p8, Va, 1'b0, n7432_1_p12
  _8x3_Priority_Encoder PE0 (
    .I7(I[7]), .I6(I[6]), .I5(I[5]), .I4(I[4]), .I3(I[3]), .I2(I[2]), .I1(I[1]), .I0(I[0]), .O2(n7432_1_p12),
    .O1(PE0_o0[1]), .O0(PE0_o0[0]), .Va(n7432_1_p2));
  _8x3_Priority_Encoder PE1 (
    .I7(I[15]), .I6(I[14]), .I5(I[13]), .I4(I[12]), .I3(I[11]), .I2(I[10]), .I1(I[9]), .I0(I[8]),
    .O2(PE1_o2), .O1(PE1_o0[1]), .O0(PE1_o0[0]), .Va(n7432_1_p3));
  _8x3_Priority_Encoder PE2 (
    .I7(I[23]), .I6(I[22]), .I5(I[21]), .I4(I[20]), .I3(I[19]), .I2(I[18]), .I1(I[17]), .I0(I[16]),
    .O2(PE2_o2), .O1(PE2_o0[1]), .O0(PE2_o0[0]), .Va(n7432_1_p7));
  _8x3_Priority_Encoder PE3 (
    .I7(I[31]), .I6(I[30]), .I5(I[29]), .I4(I[28]), .I3(I[27]), .I2(I[26]), .I1(I[25]), .I0(I[24]),
    .O2(PE3_o2), .O1(PE3_o0[1]), .O0(PE3_o0[0]), .Va(n7432_1_p6));
  _4x2_Priority_Encoder u_4x2_priority_encoder_1 (
    .I3(n7432_1_p6), .I2(n7432_1_p7), .I1(n7432_1_p3), .I0(n7432_1_p2), .O1(n4x2_priority_encoder_1_o1),
    .O0(n4x2_priority_encoder_1_o0));  // open: Va
  // _4Mux4X1 4mux4x1_1: pin names not known; wires that end beside it: 1'b0, PE1_o2, 1'b0, PE2_o2, 1'b0, PE3_o2, 1'b0, PE0_o0, PE1_o0, PE2_o0, PE3_o0, 1'b0, n4x2_priority_encoder_1_o1, n4x2_priority_encoder_1_o0, n4mux4x1_1_p15, n4mux4x1_1_p16, n4mux4x1_1_p17
  // _7404 7404_1: pin names not known; wires that end beside it: n4mux4x1_1_p16, O[0], n4mux4x1_1_p17, O[1], n4mux4x1_1_p15[0], O[2], 1'b0, 1'b1, n4x2_priority_encoder_1_o1, O[4], n4x2_priority_encoder_1_o0, O[3]
endmodule

// 4X2PE
module _4x2_Priority_Encoder (
  input  I3,
  input  I2,
  input  I1,
  input  I0,
  output O1,
  output O0,
  output Va
);

  _8x3_Priority_Encoder u_8x3_priority_encoder_1 (
    .I7(1'b0), .I6(1'b0), .I5(1'b0), .I4(1'b0), .I3(I3), .I2(I2), .I1(I1), .I0(I0), .O1(O1), .O0(O0), .Va(Va));  // open: O2
endmodule
